# Fritzing sketch HWDiagram (saved by Fritzing 0.9.9b)
breadboards: 1

parts:
  WeMos_D1_Mini1 = WeMos D1 Mini
  ESP32_-_Back1 = ESP32 - CAM
  ESP32_-_Back2 = ESP32 - CAM
  M1 = DC Motor
  M2 = DC Motor
  L298N1 = L298N DC motor driver
  VCC2 = Battery
  VCC3 = Battery

nets:
  3.3V: WeMos_D1_Mini1.3V3, ESP32_-_Back1.3.3V, ESP32_-_Back2.3.3V, VCC2.+, VCC3.+
  N1: WeMos_D1_Mini1.D7, L298N1.5V
  GND: ESP32_-_Back1.GND, ESP32_-_Back2.GND, L298N1.GND, VCC2.-, VCC3.-
  N2: M1.pin_1, L298N1.OUT4
  N3: M1.pin_2, L298N1.OUT3
  N4: M2.pin_1, L298N1.OUT2
  N5: M2.pin_2, L298N1.OUT1

custom parts:
  ESP32 - CAM: The ESP32-CAM has a very competitive small-size camera module that can operate independently as a minimum system with a footprint of only 27*40.5*4.5mm and a deep sleep current of up to 6mA.
  L298N DC motor driver: 2x DC motor driver with 78M05 positive voltage regulator (7..35 V) L298N: max 46 V, 2 A Set 5 V Enable jumper to enable 5 V regultor (needed for the L298N) and +5 V output at screw terminal or supply external +5 V at screw terminal Set ENA and/or ENB to +5 V to enable motor permanently or supply ENA and/or ENB with PWM signal IN1 and IN2 set rotation directory for motor A (OUT1/OUT2) IN2 and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
